// Digital circuit BCD.dig as structural Verilog
module BCD (
  input  clk
);

  wire and_1_out, and_2_out, and_3_out, and_4_out, FF0_nq, FF1_nq, FF2_nq, FF3_nq, or_1_out;
  wire [3:0] FF0_q;

  JK_FF FF0 (.J(1'b1), .C(clk), .K(1'b1), .Q(FF0_q[0]), .nQ(FF0_nq));
  LED ff0_2 (.in(FF0_nq));
  and and_1 (and_1_out, FF0_q[0], FF3_nq);
  JK_FF FF1 (.J(and_1_out), .C(clk), .K(and_1_out), .Q(FF0_q[1]), .nQ(FF1_nq));
  Seven_Seg_Hex seven_seg_hex_1 (.d(FF0_q), .dp(1'b0));
  LED ff1_2 (.in(FF1_nq));
  and and_2 (and_2_out, FF0_q[0], FF0_q[1]);
  JK_FF FF2 (.J(and_2_out), .C(clk), .K(and_2_out), .Q(FF0_q[2]), .nQ(FF2_nq));
  and and_3 (and_3_out, FF0_q[3], FF0_q[0]);
  and and_4 (and_4_out, and_2_out, FF0_q[2]);
  LED ff2_2 (.in(FF2_nq));
  or or_1 (or_1_out, and_3_out, and_4_out);
  JK_FF FF3 (.J(or_1_out), .C(clk), .K(or_1_out), .Q(FF0_q[3]), .nQ(FF3_nq));
  LED ff3_2 (.in(FF3_nq));
endmodule
