// Digital circuit Contadores.dig as structural Verilog
module Contadores (
  input  B,
  input  O,
  input  D,
  input  H
);

  wire and_1_out;
  wire [0:0] cnt_out;
  wire [2:0] cnt_3_out;
  wire [3:0] cnt_2_out, cnt_4_out;

  Counter #(.isProgramCounter("true")) cnt (.en(1'b1), .C(B), .clr(1'b0), .out(cnt_out[0]));  // open: ovf
  Counter #(.Bits(4)) cnt_2 (.en(1'b1), .C(D), .clr(and_1_out), .out(cnt_2_out));  // open: ovf
  Seven_Seg_Hex seven_seg_hex_1 (.d({3'b000, cnt_out[0]}), .dp(1'b0));
  Seven_Seg_Hex seven_seg_hex_2 (.d(cnt_2_out), .dp(1'b0));
  and and_1 (and_1_out, cnt_2_out[0], cnt_2_out[3]);
  Counter #(.Bits(3), .isProgramCounter("true")) cnt_3 (.en(1'b1), .C(O), .clr(1'b0), .out(cnt_3_out));  // open: ovf
  Seven_Seg_Hex seven_seg_hex_3 (.d({1'b0, cnt_3_out}), .dp(1'b0));
  Counter #(.Bits(4)) cnt_4 (.en(1'b1), .C(H), .clr(1'b0), .out(cnt_4_out));  // open: ovf
  Seven_Seg_Hex seven_seg_hex_4 (.d(cnt_4_out), .dp(1'b0));

  // Notes on the sheet:
  //   Bin
  //   Dec
  //   Oct
  //   Hex
endmodule
