// Digital circuit Conversor Analógico-Digital.dig as structural Verilog
module \Conversor_Analógico_Digital  (
  input  i,
  input  clk
);

  wire and_1_out, Btn_out, cp_eq, cp_gt, cp_lt, ct_out, ct_ovf, or_1_out, rs_ff_as_1_nq, rs_ff_as_1_q;

  Button Btn (.out(Btn_out));
  Counter ct (.en(1'b1), .C(and_1_out), .clr(Btn_out), .out(ct_out), .ovf(ct_ovf));
  RS_FF_AS rs_ff_as_1 (.S(Btn_out), .R(ct_ovf), .Q(rs_ff_as_1_q), .nQ(rs_ff_as_1_nq));
  LED ff (.in(rs_ff_as_1_nq));
  LED ovflw (.in(ct_ovf));
  Comparator cp (.a(i), .b(ct_out), .gt(cp_gt), .eq(cp_eq), .lt(cp_lt));
  Register r (.D(ct_out), .C(clk), .en(cp_eq));  // open: Q
  or or_1 (or_1_out, rs_ff_as_1_q, cp_gt, cp_lt);
  LED Or_2 (.in(or_1_out));
  and and_1 (and_1_out, clk, or_1_out);
  LED And_2 (.in(and_1_out));

  // Notes on the sheet:
  //   Relógio (clk): Fornece os pulsos de sincronismo para todo o sistema.
  //   Botão (Btn): Inicializa o ciclo de conversão, limpando o contador (clr) e definindo o estado inicial do Flip-Flop SR.
  //   Flip-Flop (ff): Atua como o "maestro" das fases. Guarda o estado da Fase 1 (quando está em SET através do botão) e transita para a Fase 2 (quando recebe o RESET vindo do overflow).
  //   Contador (ct): Mede o tempo decorrido em cada fase. Na Fase 1, conta até ao limite para gerar o tempo fixo de integração. Na Fase 2, conta até o comparador validar a igualdade.
  //   Comparador (cp): Monitoriza em tempo real quando o valor do contador (b) atinge o valor de referência ou sinal analógico digitalizado (a/i).
  //   Registo (r): Funciona como a memória de saída (Latch), capturando e congelando o valor exato do contador no instante em que o comparador sinaliza a igualdade (=).
endmodule
