// Digital circuit Gerador de texto.dig as structural Verilog
module Gerador_de_texto (
);

  wire [20:0] rom_1_d;

  ROM #(.AddrBits(7), .Bits(21)) rom_1 (.A({7{1'b0}}), .sel(1'b1), .D(rom_1_d));
  Seven_Seg seven_seg_1 (
    .a(rom_1_d[14]), .b(rom_1_d[15]), .c(rom_1_d[16]), .d(rom_1_d[17]), .e(rom_1_d[18]), .f(rom_1_d[19]),
    .g(rom_1_d[20]), .dp(1'b0));
  Seven_Seg seven_seg_2 (
    .a(rom_1_d[7]), .b(rom_1_d[8]), .c(rom_1_d[9]), .d(rom_1_d[10]), .e(rom_1_d[11]), .f(rom_1_d[12]),
    .g(rom_1_d[13]), .dp(1'b0));
  Seven_Seg seven_seg_3 (
    .a(rom_1_d[0]), .b(rom_1_d[1]), .c(rom_1_d[2]), .d(rom_1_d[3]), .e(rom_1_d[4]), .f(rom_1_d[5]),
    .g(rom_1_d[6]), .dp(1'b0));

  // Notes on the sheet:
  //   contents of rom_1 (hex, n*v repeats v):
  //   fdc77
endmodule
