// Digital circuit Lei DeMorgan.dig as structural Verilog
module Lei_DeMorgan (
  input  A,
  input  B,
  input  C,
  input  D
);

  wire [0:0] and_1_out, nor_1_out, or_1_out;

  nor nor_1 (nor_1_out[0], A, B);
  Seven_Seg_Hex seven_seg_hex_1 (.d({3'b000, nor_1_out[0]}), .dp(1'b0));
  and and_1 (and_1_out[0], nor_1_out[0], C);
  Seven_Seg_Hex seven_seg_hex_2 (.d({3'b000, and_1_out[0]}), .dp(1'b0));
  or or_1 (or_1_out[0], and_1_out[0], D);
  Seven_Seg_Hex seven_seg_hex_3 (.d({3'b000, or_1_out[0]}), .dp(1'b0));
endmodule
