// Digital circuit Lei da Soma de produtos.dig as structural Verilog
module Lei_da_Soma_de_produtos (
  input  v1,
  input  v2,
  input  v3,
  input  v4,
  input  v5
);

  wire not_1_out, not_2_out, or_1_out;
  wire [0:0] and_1_out, and_2_out, not_3_out;

  not not_1 (not_1_out, v3);
  not not_2 (not_2_out, v4);
  and and_1 (and_1_out[0], v1, v2, not_1_out);
  and and_2 (and_2_out[0], not_2_out, v5);
  Seven_Seg_Hex seven_seg_hex_1 (.d({3'b000, and_1_out[0]}), .dp(1'b0));
  Seven_Seg_Hex seven_seg_hex_2 (.d({3'b000, and_2_out[0]}), .dp(1'b0));
  or or_1 (or_1_out, and_1_out[0], and_2_out[0]);
  not not_3 (not_3_out[0], or_1_out);
  Seven_Seg_Hex seven_seg_hex_3 (.d({3'b000, not_3_out[0]}), .dp(1'b0));
endmodule
