// Digital circuit exemplo.dig as structural Verilog
module exemplo (
  input  i1,
  input  i2
);

  wire and_1_out, not_1_out, not_2_out, not_3_out, or_1_out, xor_1_out;

  and and_1 (and_1_out, i1, i2);
  or or_1 (or_1_out, i1, i2);
  xor xor_1 (xor_1_out, i2, i1);
  not not_1 (not_1_out, and_1_out);
  not not_2 (not_2_out, or_1_out);
  not not_3 (not_3_out, xor_1_out);
  LED nAnd (.in(not_1_out));
  LED And_2 (.in(and_1_out));
  LED nOr (.in(not_2_out));
  LED Or_2 (.in(or_1_out));
  LED nXor (.in(not_3_out));
  LED Xor_2 (.in(xor_1_out));
endmodule
