// Digital circuit lógica de portas.dig as structural Verilog
module \lógica_de_portas  (
  input  A1,
  input  B1,
  input  A2,
  input  B2,
  input  A3,
  input  B3,
  input  A4,
  input  B4,
  input  V1,
  input  V2,
  input  V3,
  input  V4,
  input  V5,
  input  V6,
  input  V7,
  input  V8
);

  wire and_1_out, and_2_out, and_3_out, and_4_out, and_5_out, nand_1_out, nor_1_out, not_1_out, not_2_out,
       not_3_out, not_4_out, not_5_out, not_6_out, not_7_out, not_8_out, or_1_out, or_2_out, or_3_out,
       xnor_1_out, xor_1_out;

  nand nand_1 (nand_1_out, A1, B1);
  or or_1 (or_1_out, not_1_out, not_2_out);
  not not_1 (not_1_out, A2);
  not not_2 (not_2_out, B2);
  not not_3 (not_3_out, V1);
  not not_4 (not_4_out, V2);
  not not_5 (not_5_out, V3);
  not not_6 (not_6_out, V4);
  LED led_1 (.in(nand_1_out));
  LED led_2 (.in(or_1_out));
  and and_1 (and_1_out, not_3_out, V2);
  and and_2 (and_2_out, V1, not_4_out);
  and and_3 (and_3_out, not_5_out, not_6_out);
  and and_4 (and_4_out, V3, V4);
  or or_2 (or_2_out, and_1_out, and_2_out);
  or or_3 (or_3_out, and_3_out, and_4_out);
  LED led_3 (.in(or_2_out));
  LED led_4 (.in(or_3_out));
  and and_5 (and_5_out, not_7_out, not_8_out);
  not not_7 (not_7_out, A3);
  not not_8 (not_8_out, B3);
  nor nor_1 (nor_1_out, A4, B4);
  LED led_5 (.in(nor_1_out));
  xor xor_1 (xor_1_out, V5, V6);
  xnor xnor_1 (xnor_1_out, V7, V8);
  LED led_6 (.in(and_5_out));
  LED led_7 (.in(xor_1_out));
  LED led_8 (.in(xnor_1_out));

  // Notes on the sheet:
  //   !(AxB)=!A+!B
  //   Lógica de XOR
  //   Lógica de XNOR
  //   !A+!B=!(A+B)
endmodule
