// Digital circuit relogio.dig as structural Verilog
module relogio (
  input  clk
);

  wire and_1_out, comparator_1_eq, comparator_2_eq, comparator_3_eq, comparator_4_eq, comparator_5_eq,
       comparator_6_eq, comparator_7_eq, comparator_8_eq, comparator_9_eq, comparator_10_eq,
       comparator_11_eq, comparator_12_eq, comparator_13_eq, comparator_14_eq, comparator_15_eq,
       comparator_16_eq, comparator_17_eq, comparator_18_eq;
  wire [3:0] add_1_s, add_2_s, add_3_s, add_4_s, add_5_s, add_6_s, counter_1_out, counter_2_out,
       counter_3_out, counter_4_out, counter_5_out, counter_6_out, multiplexer_1_out, multiplexer_2_out,
       multiplexer_3_out, multiplexer_4_out, multiplexer_5_out, multiplexer_6_out, register_1_q,
       register_2_q, register_3_q, register_4_q, register_5_q, register_6_q;

  Counter #(.Bits(4)) counter_1 (
    .en(1'b1), .C(comparator_4_eq), .clr(comparator_1_eq), .out(counter_1_out));  // open: ovf
  Register #(.Bits(4)) register_1 (.D(multiplexer_1_out), .C(comparator_4_eq), .en(1'b1), .Q(register_1_q));
  Comparator #(.Bits(4)) comparator_1 (.a(counter_1_out), .b(4'b0010), .eq(comparator_1_eq));  // open: gt, lt
  Add #(.Bits(4)) add_1 (.a(4'b0001), .b(register_1_q), .c_i(1'b0), .s(add_1_s));  // open: c_o
  Comparator #(.Bits(4)) comparator_2 (.a(register_1_q), .b(4'b0011), .eq(comparator_2_eq));  // open: gt, lt
  Multiplexer #(.Bits(4)) multiplexer_1 (
    .sel(comparator_2_eq), .in_0(add_1_s), .in_1(4'b0001), .out(multiplexer_1_out));
  Counter #(.Bits(4)) counter_2 (
    .en(1'b1), .C(comparator_8_eq), .clr(comparator_3_eq), .out(counter_2_out));  // open: ovf
  Register #(.Bits(4)) register_2 (.D(multiplexer_2_out), .C(comparator_8_eq), .en(1'b1), .Q(register_2_q));
  Comparator #(.Bits(4)) comparator_3 (.a(counter_2_out), .b(4'b1001), .eq(comparator_3_eq));  // open: gt, lt
  Add #(.Bits(4)) add_2 (.a(4'b0001), .b(register_2_q), .c_i(1'b0), .s(add_2_s));  // open: c_o
  Comparator #(.Bits(4)) comparator_4 (.a(register_2_q), .b(4'b1010), .eq(comparator_4_eq));  // open: gt, lt
  Comparator #(.Bits(4)) comparator_5 (.a(4'b0010), .b(counter_1_out), .eq(comparator_5_eq));  // open: gt, lt
  Multiplexer #(.Bits(4)) multiplexer_2 (
    .sel(comparator_4_eq), .in_0(add_2_s), .in_1(4'b0001), .out(multiplexer_2_out));
  Comparator #(.Bits(4)) comparator_6 (.a(4'b0011), .b(counter_2_out), .eq(comparator_6_eq));  // open: gt, lt
  Seven_Seg_Hex seven_seg_hex_1 (.d(counter_1_out), .dp(1'b0));
  Seven_Seg_Hex seven_seg_hex_2 (.d(counter_2_out), .dp(1'b0));
  Counter #(.Bits(4)) counter_3 (
    .en(1'b1), .C(comparator_11_eq), .clr(comparator_7_eq), .out(counter_3_out));  // open: ovf
  Register #(.Bits(4)) register_3 (.D(multiplexer_3_out), .C(comparator_11_eq), .en(1'b1), .Q(register_3_q));
  Comparator #(.Bits(4)) comparator_7 (.a(counter_3_out), .b(4'b0101), .eq(comparator_7_eq));  // open: gt, lt
  Comparator #(.Bits(4)) comparator_8 (.a(register_3_q), .b(4'b0110), .eq(comparator_8_eq));  // open: gt, lt
  and and_1 (and_1_out, comparator_5_eq, comparator_6_eq, comparator_9_eq, comparator_10_eq, comparator_12_eq, comparator_14_eq);
  Comparator #(.Bits(4)) comparator_9 (.a(4'b0101), .b(counter_3_out), .eq(comparator_9_eq));  // open: gt, lt
  Seven_Seg_Hex seven_seg_hex_3 (.d(counter_3_out), .dp(1'b0));
  Add #(.Bits(4)) add_3 (.a(4'b0001), .b(register_3_q), .c_i(1'b0), .s(add_3_s));  // open: c_o
  Stop stop_1 (.stop(and_1_out));
  Seven_Seg_Hex seven_seg_hex_4 (.d(counter_4_out), .dp(1'b0));
  Multiplexer #(.Bits(4)) multiplexer_3 (
    .sel(comparator_8_eq), .in_0(add_3_s), .in_1(4'b0001), .out(multiplexer_3_out));
  Comparator #(.Bits(4)) comparator_10 (.a(4'b1001), .b(counter_4_out), .eq(comparator_10_eq));  // open: gt, lt
  Seven_Seg_Hex seven_seg_hex_5 (.d(counter_5_out), .dp(1'b0));
  Counter #(.Bits(4)) counter_4 (
    .en(1'b1), .C(comparator_16_eq), .clr(comparator_13_eq), .out(counter_4_out));  // open: ovf
  Register #(.Bits(4)) register_4 (.D(multiplexer_4_out), .C(comparator_16_eq), .en(1'b1), .Q(register_4_q));
  Seven_Seg_Hex seven_seg_hex_6 (.d(counter_6_out), .dp(1'b0));
  Comparator #(.Bits(4)) comparator_11 (.a(register_4_q), .b(4'b1010), .eq(comparator_11_eq));  // open: gt, lt
  Comparator #(.Bits(4)) comparator_12 (.a(4'b0101), .b(counter_5_out), .eq(comparator_12_eq));  // open: gt, lt
  Comparator #(.Bits(4)) comparator_13 (.a(counter_4_out), .b(4'b1001), .eq(comparator_13_eq));  // open: gt, lt
  Add #(.Bits(4)) add_4 (.a(4'b0001), .b(register_4_q), .c_i(1'b0), .s(add_4_s));  // open: c_o
  Multiplexer #(.Bits(4)) multiplexer_4 (
    .sel(comparator_11_eq), .in_0(add_4_s), .in_1(4'b0001), .out(multiplexer_4_out));
  Comparator #(.Bits(4)) comparator_14 (.a(4'b1001), .b(counter_6_out), .eq(comparator_14_eq));  // open: gt, lt
  Counter #(.Bits(4)) counter_5 (
    .en(1'b1), .C(comparator_18_eq), .clr(comparator_15_eq), .out(counter_5_out));  // open: ovf
  Register #(.Bits(4)) register_5 (.D(multiplexer_5_out), .C(comparator_18_eq), .en(1'b1), .Q(register_5_q));
  Comparator #(.Bits(4)) comparator_15 (.a(counter_5_out), .b(4'b0101), .eq(comparator_15_eq));  // open: gt, lt
  Add #(.Bits(4)) add_5 (.a(4'b0001), .b(register_5_q), .c_i(1'b0), .s(add_5_s));  // open: c_o
  Comparator #(.Bits(4)) comparator_16 (.a(register_5_q), .b(4'b0110), .eq(comparator_16_eq));  // open: gt, lt
  Multiplexer #(.Bits(4)) multiplexer_5 (
    .sel(comparator_16_eq), .in_0(add_5_s), .in_1(4'b0001), .out(multiplexer_5_out));
  Counter #(.Bits(4)) counter_6 (.en(1'b1), .C(clk), .clr(comparator_17_eq), .out(counter_6_out));  // open: ovf
  Register #(.Bits(4)) register_6 (.D(multiplexer_6_out), .C(clk), .en(1'b1), .Q(register_6_q));
  Comparator #(.Bits(4)) comparator_17 (.a(counter_6_out), .b(4'b1001), .eq(comparator_17_eq));  // open: gt, lt
  Add #(.Bits(4)) add_6 (.a(4'b0001), .b(register_6_q), .c_i(1'b0), .s(add_6_s));  // open: c_o
  Comparator #(.Bits(4)) comparator_18 (.a(register_6_q), .b(4'b1010), .eq(comparator_18_eq));  // open: gt, lt
  Multiplexer #(.Bits(4)) multiplexer_6 (
    .sel(comparator_18_eq), .in_0(add_6_s), .in_1(4'b0001), .out(multiplexer_6_out));
endmodule
