// Digital circuit sincronizacao de flip flop.dig as structural Verilog
module sincronizacao_de_flip_flop (
  input  Clk,
  input  I_O
);

  wire and_1_out, and_2_out, and_3_out, and_4_out, FF1_nq, FF1_q, FF2_nq, FF2_q, FF3_nq, FF3_q, not_1_out,
       or_1_out, or_2_out;

  JK_FF FF1 (.J(1'b1), .C(Clk), .K(1'b1), .Q(FF1_q), .nQ(FF1_nq));
  not not_1 (not_1_out, I_O);
  LED off1u (.in(FF1_q));
  and and_1 (and_1_out, I_O, FF1_q);
  and and_2 (and_2_out, FF1_nq, not_1_out);
  LED off1d (.in(FF1_nq));
  or or_1 (or_1_out, and_1_out, and_2_out);
  JK_FF FF2 (.J(or_1_out), .C(Clk), .K(or_1_out), .Q(FF2_q), .nQ(FF2_nq));
  LED off2u (.in(FF2_q));
  and and_3 (and_3_out, and_1_out, FF2_q);
  and and_4 (and_4_out, FF2_nq, and_2_out);
  LED off2d (.in(FF2_nq));
  or or_2 (or_2_out, and_3_out, and_4_out);
  JK_FF FF3 (.J(or_2_out), .C(Clk), .K(or_2_out), .Q(FF3_q), .nQ(FF3_nq));
  LED off3u (.in(FF3_q));
  LED off3d (.in(FF3_nq));
endmodule
